# Fritzing sketch FoggerShield (saved by Fritzing 0.7.12b)
perfboards: 1

parts:
  Arduino1 = Arduino  # not connected
  J13 = male pin header, 4 pins [form="♂ (male)"]
  J14 = male pin header, 2 pins [form="♂ (male)"]
  J16 = male pin header, 3 pins [form="♂ (male)"]
  J18 = male pin header, 3 pins [form="♂ (male)"]
  J17 = male pin header, 3 pins [form="♂ (male)"]
  J10 = male pin header, 3 pins [form="♂ (male)"]
  J8 = male pin header, 3 pins [form="♂ (male)"]
  J9 = male pin header, 3 pins [form="♂ (male)"]
  J7 = male pin header, 4 pins [form="♂ (male)"]
  J2 = male pin header, 6 pins [form="♂ (male)"]
  J11 = male pin header, 6 pins [form="♂ (male)"]
  J12 = male pin header, 6 pins [form="♂ (male)"]  # not connected
  J1 = male pin header, 6 pins [form="♂ (male)"]
  J20 = male pin header, 3 pins [form="♂ (male)"]
  U1 = mystery part, 6 pins [chip_label=N-CH-MOS]
  J21 = male pin header, 2 pins [form="♂ (male)"]
  J22 = male pin header, 2 pins [form="♂ (male)"]
  J23 = male pin header, 2 pins [form="♂ (male)"]
  R1 = Resistor [tolerance=±5% resistance=10k package=THT]
  J25 = male pin header, 1 pin [form="♂ (male)"]
  J26 = male pin header, 1 pin [form="♂ (male)"]
  J28 = male pin header, 2 pins [form="♂ (male)"]
  J30 = male pin header, 1 pin [form="♂ (male)"]
  J31 = male pin header, 1 pin [form="♂ (male)"]
  J33 = male pin header, 1 pin [form="♂ (male)"]
  J34 = male pin header, 1 pin [form="♂ (male)"]
  J35 = male pin header, 1 pin [form="♂ (male)"]
  J36 = male pin header, 1 pin [form="♂ (male)"]
  J38 = male pin header, 1 pin [form="♂ (male)"]  # not connected
  J39 = male pin header, 1 pin [form="♂ (male)"]  # not connected
  J40 = male pin header, 1 pin [form="♂ (male)"]  # not connected
  J41 = male pin header, 1 pin [form="♂ (male)"]  # not connected
  J42 = male pin header, 1 pin [form="♂ (male)"]  # not connected
  J43 = male pin header, 1 pin [form="♂ (male)"]  # not connected
  J45 = male pin header, 1 pin [form="♂ (male)"]  # not connected
  J47 = male pin header, 1 pin [form="♂ (male)"]  # not connected
  R2 = Resistor [tolerance=±5% resistance=10k package=THT]
  R3 = Resistor [tolerance=±5% resistance=10k package=THT]
  R4 = Resistor [tolerance=±5% resistance=10k package=THT]
  D1 = Rectifier Diode [part_number=1N4001 package="300 mil [THT]"]
  J48 = male pin header, 1 pin [form="♂ (male)"]
  J49 = male pin header, 1 pin [form="♂ (male)"]  # not connected
  J50 = male pin header, 3 pins [form="♂ (male)"]
  R5 = Resistor [tolerance=±5% resistance=10k package=THT]
  J51 = male pin header, 2 pins [form="♂ (male)"]
  R6 = Resistor [tolerance=±5% resistance=10k package=THT]

nets:
  N1: J13.pin1, J33.pin1
  N2: J13.pin2, J34.pin1
  N3: J13.pin3, J35.pin1
  N4: J13.pin4, J36.pin1
  N5: J14.pin1, J16.pin2, R1.Pin_0
  N6: J14.pin2, J16.pin1, R6.Pin_0
  N7: J16.pin3, R1.Pin_1, J26.pin1
  N8: J18.pin1, R3.Pin_0
  N9: J18.pin3, J31.pin1, R3.Pin_1
  N10: J17.pin2, R2.Pin_0
  N11: J17.pin3, J30.pin1, R2.Pin_1
  N12: J10.pin1, J2.pin2
  N13: J8.pin1, J2.pin3
  N14: J9.pin1, J2.pin4
  N15: J7.pin1, J2.pin6
  N16: J7.pin2, J2.pin5
  N17: J7.pin3, J1.pin3
  N18: J7.pin4, J1.pin4
  N19: J2.pin1, J20.pin1
  N20: J11.pin1, R4.Pin_0
  N21: J1.pin1, J28.pin1
  N22: J1.pin5, J51.pin1
  N23: J1.pin6, J51.pin2
  N24: J20.pin3, R4.Pin_1
  N25: U1.pin1, U1.pin3, J21.pin1
  N26: U1.pin4, J25.pin1, R6.Pin_1
  N27: U1.pin6, J22.pin2, D1.anode
  N28: J21.pin2, J23.pin1
  N29: J22.pin1, J23.pin2, D1.cathode
  N30: J28.pin2, J50.pin1, R5.Pin_0
  N31: J48.pin1, J50.pin3, R5.Pin_1

notes:
  RST
  3V3
  5V
  GND
  VIN
  Backlight Button A0
  Pot 1 A1
  Pot 3 A3
  LCD A5
  LCD A4
  Pot 2 A2
  D0 Relay 1
  D1 Relay 2
  D2 Relay 3
  D3 Relay 4
  D4
  D5 Floatswitch
  D6 Humidity
  D7
  D8 Unused/Filler Floatswitch
  D9 Temp
  D10
  D11 Fan
  D12
  Fan
  +12 In
  To Relay
  Reset Button
  +7-9
